# Fritzing sketch rgbstripard (saved by Fritzing 0.9.4)
breadboards: 1

parts:
  Part1 = Arduino Nano (Rev3.0)
  U1 = WS2812 RGB LED strip
  C1 = Capacitor Polarized [package=panasonic_d]
  S1 = Pushbutton [package="[SMD]"]
  R1 = PHOTOCELL [package=photocell-kit]
  R2 = Resistor [tolerance=±5% resistance=10k package="0402 [SMD]"]

nets:
  GND: Part1.GND, Part1.D13/SCK, U1.GND, C1.-, S1.Pin_1, S1.Pin_2, R1.P$2
  N1: Part1.D2, U1.DIN
  N2: Part1.D6, S1.Pin_3, S1.Pin_4
  5V: Part1.5V, U1.VCC, C1.+, R2.Pin_0
  N3: Part1.A0, R1.P$1, R2.Pin_1

custom parts:
  WS2812 RGB LED strip: WS2812 strip
